// Logisim project finalproject.circ as structural Verilog: 10 circuits, main circuit main
module main (
);

  wire alarm_1_am, alarm_1_m0_2, alarm_1_m1_2, alarm_1_m2_2, alarm_1_out, alarm_1_pm, alarm_1_q0_2,
       alarm_1_q1_2, alarm_1_q2_2, alarm_1_q3_2, alarm_1_s0_2, alarm_1_s1_2, alarm_1_s2_2, alarm_1_s3_2,
       and_1_out, and_2_out, and_3_out, binary_to_7_seg_decoder_1_qa, binary_to_7_seg_decoder_1_qb,
       binary_to_7_seg_decoder_1_qc, binary_to_7_seg_decoder_1_qd, binary_to_7_seg_decoder_1_qe,
       binary_to_7_seg_decoder_1_qf, binary_to_7_seg_decoder_1_qg, binary_to_7_seg_decoder_2_qa,
       binary_to_7_seg_decoder_2_qb, binary_to_7_seg_decoder_2_qc, binary_to_7_seg_decoder_2_qd,
       binary_to_7_seg_decoder_2_qe, binary_to_7_seg_decoder_2_qf, binary_to_7_seg_decoder_2_qg, clock_1_out,
       clock_2_out, hour_decoder_1_qa0, hour_decoder_1_qa1, hour_decoder_1_qb0, hour_decoder_1_qb1,
       hour_decoder_1_qc0, hour_decoder_1_qc1, hour_decoder_1_qd0, hour_decoder_1_qd1, hour_decoder_1_qe0,
       hour_decoder_1_qe1, hour_decoder_1_qf0, hour_decoder_1_qf1, hour_decoder_1_qg0, hour_decoder_1_qg1,
       ON_OFF_2_out, ON_OFF_out, RESET_2_out, RESET_out, SET_DAYS_out, Set_HOURS_2_out, SET_HOURS_out,
       Set_MINUTES_2_out, SET_MINUTES_out, START_out, STOP_WATCH_out_8, STOP_WATCH_out_9, STOP_WATCH_out_10,
       STOP_WATCH_out_11, STOP_WATCH_out_12, STOP_WATCH_out_13, STOP_WATCH_out_14, STOP_WATCH_out_15,
       STOP_WATCH_out_16, STOP_WATCH_out_17, STOP_WATCH_out_18, STOP_WATCH_out_19, STOP_WATCH_out_20,
       STOP_WATCH_out_21, STOP_WATCH_out_22, STOP_WATCH_out_23, STOP_WATCH_out_24, STOP_WATCH_out_25,
       STOP_WATCH_out_26, STOP_WATCH_out_27, STOP_WATCH_out_28, STOP_WATCH_out_29, STOP_WATCH_out_30,
       STOP_WATCH_out_31, STOP_WATCH_out_34, STOP_WATCH_out_35, STOP_WATCH_out_36, STOP_WATCH_out_37,
       STOP_WATCH_out_38, STOP_WATCH_out_39, STOP_WATCH_out_40, STOP_WATCH_out_41, STOP_WATCH_out_42,
       STOP_WATCH_out_43, STOP_WATCH_out_44, STOP_WATCH_out_45, STOP_WATCH_out_46, STOP_WATCH_out_47,
       STOP_WATCH_out_48, STOP_WATCH_out_49, STOP_WATCH_out_50, STOP_WATCH_out_51, t_ff_1_q, t_ff_2_q,
       t_ff_3_q, THE_CLOCK_am, THE_CLOCK_am_2, THE_CLOCK_fri, THE_CLOCK_m0, THE_CLOCK_m1, THE_CLOCK_m2,
       THE_CLOCK_mon, THE_CLOCK_out_8, THE_CLOCK_out_9, THE_CLOCK_out_10, THE_CLOCK_out_11, THE_CLOCK_out_12,
       THE_CLOCK_out_13, THE_CLOCK_out_14, THE_CLOCK_out_15, THE_CLOCK_out_16, THE_CLOCK_out_17,
       THE_CLOCK_out_18, THE_CLOCK_out_19, THE_CLOCK_out_20, THE_CLOCK_out_21, THE_CLOCK_out_22,
       THE_CLOCK_out_23, THE_CLOCK_out_24, THE_CLOCK_out_25, THE_CLOCK_out_26, THE_CLOCK_out_27,
       THE_CLOCK_out_28, THE_CLOCK_out_29, THE_CLOCK_out_30, THE_CLOCK_out_31, THE_CLOCK_out_34,
       THE_CLOCK_out_35, THE_CLOCK_out_36, THE_CLOCK_out_37, THE_CLOCK_out_38, THE_CLOCK_out_39,
       THE_CLOCK_out_40, THE_CLOCK_out_41, THE_CLOCK_out_42, THE_CLOCK_out_43, THE_CLOCK_out_44,
       THE_CLOCK_out_45, THE_CLOCK_out_46, THE_CLOCK_out_47, THE_CLOCK_out_48, THE_CLOCK_out_49,
       THE_CLOCK_out_50, THE_CLOCK_out_51, THE_CLOCK_pm, THE_CLOCK_q0, THE_CLOCK_q1, THE_CLOCK_q2,
       THE_CLOCK_q3, THE_CLOCK_s0, THE_CLOCK_s1, THE_CLOCK_s2, THE_CLOCK_s3, THE_CLOCK_sat, THE_CLOCK_sun,
       THE_CLOCK_thrus, THE_CLOCK_tues, THE_CLOCK_wends;

  LED FRI (.in(THE_CLOCK_fri));
  LED THU (.in(THE_CLOCK_thrus));
  LED WED (.in(THE_CLOCK_wends));
  LED TUE (.in(THE_CLOCK_tues));
  LED MON (.in(THE_CLOCK_mon));
  LED SUN (.in(THE_CLOCK_sun));
  LED SAT (.in(THE_CLOCK_sat));
  Button RESET (.out(RESET_out));
  Button START (.out(START_out));
  LED AM (.in(THE_CLOCK_am));
  T_Flip_Flop t_ff_1 (.clk(START_out), .T(1'b1), .Q(t_ff_1_q));  // open: Qn, preset, reset, en
  LED PM (.in(THE_CLOCK_pm));
  Button SET_DAYS (.out(SET_DAYS_out));
  Button SET_HOURS (.out(SET_HOURS_out));
  Button SET_MINUTES (.out(SET_MINUTES_out));
  CLOCK THE_CLOCK (
    .Fri(THE_CLOCK_fri), .Thrus(THE_CLOCK_thrus), .Wends(THE_CLOCK_wends), .Tues(THE_CLOCK_tues),
    .Mon(THE_CLOCK_mon), .Sun(THE_CLOCK_sun), .Sat(THE_CLOCK_sat), .CLK_IN(and_2_out),
    .out_34(THE_CLOCK_out_34), .out_35(THE_CLOCK_out_35), .out_36(THE_CLOCK_out_36),
    .out_37(THE_CLOCK_out_37), .out_38(THE_CLOCK_out_38), .out_39(THE_CLOCK_out_39),
    .out_40(THE_CLOCK_out_40), .out_41(THE_CLOCK_out_41), .out_42(THE_CLOCK_out_42),
    .out_43(THE_CLOCK_out_43), .out_44(THE_CLOCK_out_44), .out_45(THE_CLOCK_out_45),
    .out_46(THE_CLOCK_out_46), .out_47(THE_CLOCK_out_47), .out_48(THE_CLOCK_out_48),
    .out_49(THE_CLOCK_out_49), .out_50(THE_CLOCK_out_50), .out_51(THE_CLOCK_out_51), .Set_Days(SET_DAYS_out),
    .AM_2(THE_CLOCK_am_2), .out_8(THE_CLOCK_out_8), .Q3(THE_CLOCK_q3), .out_9(THE_CLOCK_out_9),
    .out_10(THE_CLOCK_out_10), .out_11(THE_CLOCK_out_11), .Q2(THE_CLOCK_q2), .out_12(THE_CLOCK_out_12),
    .out_13(THE_CLOCK_out_13), .out_14(THE_CLOCK_out_14), .out_15(THE_CLOCK_out_15), .Q1(THE_CLOCK_q1),
    .Q0(THE_CLOCK_q0), .m2(THE_CLOCK_m2), .Set_Hours(SET_HOURS_out), .out_16(THE_CLOCK_out_16),
    .out_17(THE_CLOCK_out_17), .m1(THE_CLOCK_m1), .out_18(THE_CLOCK_out_18), .out_19(THE_CLOCK_out_19),
    .m0(THE_CLOCK_m0), .s3(THE_CLOCK_s3), .s2(THE_CLOCK_s2), .out_20(THE_CLOCK_out_20),
    .out_21(THE_CLOCK_out_21), .out_22(THE_CLOCK_out_22), .out_23(THE_CLOCK_out_23), .s1(THE_CLOCK_s1),
    .s0(THE_CLOCK_s0), .Set_Minutes(SET_MINUTES_out), .out_24(THE_CLOCK_out_24), .out_25(THE_CLOCK_out_25),
    .out_26(THE_CLOCK_out_26), .out_27(THE_CLOCK_out_27), .out_28(THE_CLOCK_out_28),
    .out_29(THE_CLOCK_out_29), .out_30(THE_CLOCK_out_30), .out_31(THE_CLOCK_out_31), .PM(THE_CLOCK_pm),
    .AM(THE_CLOCK_am));  // open: RESET
  _7_Segment_Display u_7_segment_display_1 (
    .g(THE_CLOCK_out_8), .f(THE_CLOCK_out_9), .a(THE_CLOCK_out_10), .b(THE_CLOCK_out_11),
    .e(THE_CLOCK_out_34), .d(THE_CLOCK_out_35), .c(THE_CLOCK_out_36));  // open: dp
  _7_Segment_Display u_7_segment_display_2 (
    .g(THE_CLOCK_out_12), .f(THE_CLOCK_out_13), .a(THE_CLOCK_out_14), .b(THE_CLOCK_out_15),
    .e(THE_CLOCK_out_37), .d(THE_CLOCK_out_38), .c(THE_CLOCK_out_39));  // open: dp
  CLOCK STOP_WATCH (
    .CLK_IN(and_1_out), .out_34(STOP_WATCH_out_34), .out_35(STOP_WATCH_out_35), .out_36(STOP_WATCH_out_36),
    .out_37(STOP_WATCH_out_37), .out_38(STOP_WATCH_out_38), .out_39(STOP_WATCH_out_39),
    .out_40(STOP_WATCH_out_40), .out_41(STOP_WATCH_out_41), .out_42(STOP_WATCH_out_42),
    .out_43(STOP_WATCH_out_43), .out_44(STOP_WATCH_out_44), .out_45(STOP_WATCH_out_45),
    .out_46(STOP_WATCH_out_46), .out_47(STOP_WATCH_out_47), .out_48(STOP_WATCH_out_48),
    .out_49(STOP_WATCH_out_49), .out_50(STOP_WATCH_out_50), .out_51(STOP_WATCH_out_51),
    .out_8(STOP_WATCH_out_8), .out_9(STOP_WATCH_out_9), .out_10(STOP_WATCH_out_10),
    .out_11(STOP_WATCH_out_11), .out_12(STOP_WATCH_out_12), .out_13(STOP_WATCH_out_13),
    .out_14(STOP_WATCH_out_14), .out_15(STOP_WATCH_out_15), .out_16(STOP_WATCH_out_16),
    .out_17(STOP_WATCH_out_17), .out_18(STOP_WATCH_out_18), .out_19(STOP_WATCH_out_19),
    .out_20(STOP_WATCH_out_20), .out_21(STOP_WATCH_out_21), .out_22(STOP_WATCH_out_22),
    .out_23(STOP_WATCH_out_23), .out_24(STOP_WATCH_out_24), .out_25(STOP_WATCH_out_25),
    .out_26(STOP_WATCH_out_26), .out_27(STOP_WATCH_out_27), .out_28(STOP_WATCH_out_28),
    .out_29(STOP_WATCH_out_29), .out_30(STOP_WATCH_out_30), .out_31(STOP_WATCH_out_31), .RESET(RESET_out));  // open: Fri, Thrus, Wends, Tues, Mon, Sun, Sat, Set_Days, AM_2, Q3, Q2, Q1, Q0, m2, Set_Hours, m1, m0, s3, s2, s1, s0, Set_Minutes, PM, AM
  _7_Segment_Display u_7_segment_display_3 (
    .g(STOP_WATCH_out_12), .f(STOP_WATCH_out_13), .a(STOP_WATCH_out_14), .b(STOP_WATCH_out_15),
    .e(STOP_WATCH_out_37), .d(STOP_WATCH_out_38), .c(STOP_WATCH_out_39));  // open: dp
  _7_Segment_Display u_7_segment_display_4 (
    .g(STOP_WATCH_out_8), .f(STOP_WATCH_out_9), .a(STOP_WATCH_out_10), .b(STOP_WATCH_out_11),
    .e(STOP_WATCH_out_34), .d(STOP_WATCH_out_35), .c(STOP_WATCH_out_36));  // open: dp
  _7_Segment_Display u_7_segment_display_5 (
    .g(THE_CLOCK_out_16), .f(THE_CLOCK_out_17), .a(THE_CLOCK_out_18), .b(THE_CLOCK_out_19),
    .e(THE_CLOCK_out_40), .d(THE_CLOCK_out_41), .c(THE_CLOCK_out_42));  // open: dp
  _7_Segment_Display u_7_segment_display_6 (
    .g(STOP_WATCH_out_16), .f(STOP_WATCH_out_17), .a(STOP_WATCH_out_18), .b(STOP_WATCH_out_19),
    .e(STOP_WATCH_out_40), .d(STOP_WATCH_out_41), .c(STOP_WATCH_out_42));  // open: dp
  Button ON_OFF (.out(ON_OFF_out));
  _7_Segment_Display u_7_segment_display_7 (
    .g(THE_CLOCK_out_24), .f(THE_CLOCK_out_25), .a(THE_CLOCK_out_26), .b(THE_CLOCK_out_27),
    .e(THE_CLOCK_out_46), .d(THE_CLOCK_out_47), .c(THE_CLOCK_out_48));  // open: dp
  _7_Segment_Display u_7_segment_display_8 (
    .g(THE_CLOCK_out_20), .f(THE_CLOCK_out_21), .a(THE_CLOCK_out_22), .b(THE_CLOCK_out_23),
    .e(THE_CLOCK_out_43), .d(THE_CLOCK_out_44), .c(THE_CLOCK_out_45));  // open: dp
  _7_Segment_Display u_7_segment_display_9 (
    .g(STOP_WATCH_out_20), .f(STOP_WATCH_out_21), .a(STOP_WATCH_out_22), .b(STOP_WATCH_out_23),
    .e(STOP_WATCH_out_43), .d(STOP_WATCH_out_44), .c(STOP_WATCH_out_45));  // open: dp
  _7_Segment_Display u_7_segment_display_10 (
    .g(STOP_WATCH_out_24), .f(STOP_WATCH_out_25), .a(STOP_WATCH_out_26), .b(STOP_WATCH_out_27),
    .e(STOP_WATCH_out_46), .d(STOP_WATCH_out_47), .c(STOP_WATCH_out_48));  // open: dp
  _7_Segment_Display u_7_segment_display_11 (
    .g(THE_CLOCK_out_28), .f(THE_CLOCK_out_29), .a(THE_CLOCK_out_30), .b(THE_CLOCK_out_31),
    .e(THE_CLOCK_out_49), .d(THE_CLOCK_out_50), .c(THE_CLOCK_out_51));  // open: dp
  _7_Segment_Display u_7_segment_display_12 (
    .g(STOP_WATCH_out_28), .f(STOP_WATCH_out_29), .a(STOP_WATCH_out_30), .b(STOP_WATCH_out_31),
    .e(STOP_WATCH_out_49), .d(STOP_WATCH_out_50), .c(STOP_WATCH_out_51));  // open: dp
  and and_1 (and_1_out, and_2_out, t_ff_1_q);
  T_Flip_Flop t_ff_2 (.clk(ON_OFF_out), .T(1'b1), .Q(t_ff_2_q));  // open: Qn, preset, reset, en
  Clock clock_1 (.out(clock_1_out));
  and and_2 (and_2_out, t_ff_2_q, clock_1_out);
  LED ALARM_ON (.in(t_ff_3_q));
  Button ON_OFF_2 (.out(ON_OFF_2_out));
  Button Set_HOURS_2 (.out(Set_HOURS_2_out));
  Button Set_MINUTES_2 (.out(Set_MINUTES_2_out));
  Button RESET_2 (.out(RESET_2_out));
  T_Flip_Flop t_ff_3 (.clk(ON_OFF_2_out), .T(1'b1), .Q(t_ff_3_q));  // open: Qn, preset, reset, en
  Alarm alarm_1 (
    .S3(THE_CLOCK_s3), .M1(THE_CLOCK_m1), .M2(THE_CLOCK_m2), .S2(THE_CLOCK_s2), .Q1(THE_CLOCK_q1),
    .M0(THE_CLOCK_m0), .Q3(THE_CLOCK_q3), .Q0(THE_CLOCK_q0), .S1(THE_CLOCK_s1), .S0(THE_CLOCK_s0),
    .Q2(THE_CLOCK_q2), .AM(alarm_1_am), .PM(alarm_1_pm), .RESET(RESET_2_out), .OUT(alarm_1_out),
    .q0_2(alarm_1_q0_2), .q1_2(alarm_1_q1_2), .q2_2(alarm_1_q2_2), .q3_2(alarm_1_q3_2), .s0_2(alarm_1_s0_2),
    .s1_2(alarm_1_s1_2), .s2_2(alarm_1_s2_2), .s3_2(alarm_1_s3_2), .m0_2(alarm_1_m0_2), .m1_2(alarm_1_m1_2),
    .m2_2(alarm_1_m2_2), .Am_IN(THE_CLOCK_am_2), .Set_Minutes(Set_MINUTES_2_out),
    .Set_Hours(Set_HOURS_2_out), .ON_OFF(t_ff_3_q));
  LED AM_2 (.in(alarm_1_am));
  LED PM_2 (.in(alarm_1_pm));
  LED WAKE_UP (.in(and_3_out));
  and and_3 (and_3_out, alarm_1_out, clock_2_out);
  Clock clock_2 (.out(clock_2_out));
  _7_Segment_Display u_7_segment_display_13 (
    .g(hour_decoder_1_qg1), .f(hour_decoder_1_qf1), .a(hour_decoder_1_qa1), .b(hour_decoder_1_qb1),
    .e(hour_decoder_1_qe1), .d(hour_decoder_1_qd1), .c(hour_decoder_1_qc1));  // open: dp
  Hour_Decoder hour_decoder_1 (
    .QA1(hour_decoder_1_qa1), .QB1(hour_decoder_1_qb1), .QC1(hour_decoder_1_qc1), .QD1(hour_decoder_1_qd1),
    .QE1(hour_decoder_1_qe1), .QF1(hour_decoder_1_qf1), .QG1(hour_decoder_1_qg1), .QA0(hour_decoder_1_qa0),
    .QB0(hour_decoder_1_qb0), .QC0(hour_decoder_1_qc0), .QD0(hour_decoder_1_qd0), .QE0(hour_decoder_1_qe0),
    .QF0(hour_decoder_1_qf0), .QG0(hour_decoder_1_qg0), .I3(alarm_1_q3_2), .I2(alarm_1_q2_2),
    .I1(alarm_1_q1_2), .I0(alarm_1_q0_2));
  _7_Segment_Display u_7_segment_display_14 (
    .g(hour_decoder_1_qg0), .f(hour_decoder_1_qf0), .a(hour_decoder_1_qa0), .b(hour_decoder_1_qb0),
    .e(hour_decoder_1_qe0), .d(hour_decoder_1_qd0), .c(hour_decoder_1_qc0));  // open: dp
  _7_Segment_Display u_7_segment_display_15 (
    .g(binary_to_7_seg_decoder_1_qg), .f(binary_to_7_seg_decoder_1_qf), .a(binary_to_7_seg_decoder_1_qa),
    .b(binary_to_7_seg_decoder_1_qb), .e(binary_to_7_seg_decoder_1_qe), .d(binary_to_7_seg_decoder_1_qd),
    .c(binary_to_7_seg_decoder_1_qc));  // open: dp
  Binary_to_7_Seg_Decoder binary_to_7_seg_decoder_1 (
    .QA(binary_to_7_seg_decoder_1_qa), .QB(binary_to_7_seg_decoder_1_qb), .QC(binary_to_7_seg_decoder_1_qc),
    .QD(binary_to_7_seg_decoder_1_qd), .QE(binary_to_7_seg_decoder_1_qe), .QF(binary_to_7_seg_decoder_1_qf),
    .QG(binary_to_7_seg_decoder_1_qg), .I3(1'b0), .I2(alarm_1_m2_2), .I1(alarm_1_m1_2), .I0(alarm_1_m0_2));
  _7_Segment_Display u_7_segment_display_16 (
    .g(binary_to_7_seg_decoder_2_qg), .f(binary_to_7_seg_decoder_2_qf), .a(binary_to_7_seg_decoder_2_qa),
    .b(binary_to_7_seg_decoder_2_qb), .e(binary_to_7_seg_decoder_2_qe), .d(binary_to_7_seg_decoder_2_qd),
    .c(binary_to_7_seg_decoder_2_qc));  // open: dp
  Binary_to_7_Seg_Decoder binary_to_7_seg_decoder_2 (
    .QA(binary_to_7_seg_decoder_2_qa), .QB(binary_to_7_seg_decoder_2_qb), .QC(binary_to_7_seg_decoder_2_qc),
    .QD(binary_to_7_seg_decoder_2_qd), .QE(binary_to_7_seg_decoder_2_qe), .QF(binary_to_7_seg_decoder_2_qf),
    .QG(binary_to_7_seg_decoder_2_qg), .I3(alarm_1_s3_2), .I2(alarm_1_s2_2), .I1(alarm_1_s1_2),
    .I0(alarm_1_s0_2));

  // Notes on the sheet:
  //   THE CLOCK SWITCH
  //   DIGITAL CLOCK
  //   THE ALARM
endmodule

// 0-9 r
module _0_9_Counter (
  input  Clk_In,
  input  RESET,
  output Q3,
  output Q2,
  output Q1,
  output Q0,
  output Clk_Out
);

  wire and_2_out, and_3_out, and_4_out, and_5_out, or_1_out, t_ff_1_qn, t_ff_2_qn, t_ff_3_qn, t_ff_4_qn;

  and and_1 (Clk_Out, t_ff_1_qn, t_ff_2_qn, t_ff_3_qn, t_ff_4_qn);
  or or_1 (or_1_out, and_2_out, and_3_out);
  and and_2 (and_2_out, Q0, Q1, Q2);
  T_Flip_Flop t_ff_1 (.clk(Clk_In), .T(or_1_out), .Q(Q3), .Qn(t_ff_1_qn), .reset(RESET));  // open: preset, en
  and and_3 (and_3_out, Q0, Q3);
  and and_4 (and_4_out, Q0, Q1);
  T_Flip_Flop t_ff_2 (.clk(Clk_In), .T(and_4_out), .Q(Q2), .Qn(t_ff_2_qn), .reset(RESET));  // open: preset, en
  and and_5 (and_5_out, t_ff_1_qn, Q0);
  T_Flip_Flop t_ff_3 (.clk(Clk_In), .T(and_5_out), .Q(Q1), .Qn(t_ff_3_qn), .reset(RESET));  // open: preset, en
  T_Flip_Flop t_ff_4 (.clk(Clk_In), .T(1'b1), .Q(Q0), .Qn(t_ff_4_qn), .reset(RESET));  // open: preset, en
endmodule

// 0-5
module _0_5_Counter (
  input  Clk_In,
  input  RESET,
  output Q2,
  output Q1,
  output Q0,
  output Clk_Out
);

  wire and_2_out, and_3_out, or_1_out, t_ff_1_qn, t_ff_2_qn, t_ff_3_qn;

  and and_1 (Clk_Out, t_ff_1_qn, t_ff_2_qn, t_ff_3_qn);
  and and_2 (and_2_out, or_1_out, Q0);
  or or_1 (or_1_out, Q1, Q2);
  T_Flip_Flop t_ff_1 (.clk(Clk_In), .T(and_2_out), .Q(Q2), .Qn(t_ff_1_qn), .reset(RESET));  // open: preset, en
  T_Flip_Flop t_ff_2 (.clk(Clk_In), .T(and_3_out), .Q(Q1), .Qn(t_ff_2_qn), .reset(RESET));  // open: preset, en
  and and_3 (and_3_out, t_ff_1_qn, Q0);
  T_Flip_Flop t_ff_3 (.clk(Clk_In), .T(1'b1), .Q(Q0), .Qn(t_ff_3_qn), .reset(RESET));  // open: preset, en
endmodule

// Decoder
module Binary_to_7_Seg_Decoder (
  input  I3,
  input  I2,
  input  I1,
  input  I0,
  output QA,
  output QB,
  output QC,
  output QD,
  output QE,
  output QF,
  output QG
);

  wire and_1_out, and_2_out, and_3_out, and_4_out, and_5_out, and_6_out, and_7_out, and_8_out, and_9_out,
       and_10_out, and_11_out, not_1_out, not_2_out, not_3_out, not_4_out, or_1_out, or_2_out, or_3_out,
       or_4_out;

  not not_1 (not_1_out, I3);
  not not_2 (not_2_out, I2);
  not not_3 (not_3_out, I0);
  not not_4 (not_4_out, I1);
  and and_1 (and_1_out, I2, I0);
  and and_2 (and_2_out, not_2_out, not_3_out);
  and and_3 (and_3_out, I1, I0);
  and and_4 (and_4_out, not_4_out, not_3_out);
  or or_1 (or_1_out, I1, not_2_out);
  and and_5 (and_5_out, or_1_out, not_3_out);
  and and_6 (and_6_out, I0, not_4_out, I2);
  and and_7 (and_7_out, I1, not_2_out);
  or or_2 (or_2_out, I1, not_2_out);
  or or_3 (or_3_out, not_3_out, not_4_out);
  and and_8 (and_8_out, or_3_out, I2);
  and and_9 (and_9_out, not_3_out, not_4_out);
  or or_4 (or_4_out, not_3_out, not_4_out);
  and and_10 (and_10_out, or_4_out, I2);
  and and_11 (and_11_out, I1, not_2_out);
  or or_5 (QA, and_1_out, and_2_out, I3, I1);
  or or_6 (QB, and_3_out, and_4_out, not_2_out);
  or or_7 (QC, I2, not_4_out, I0);
  or or_8 (QD, and_5_out, and_6_out, and_7_out, I3);
  and and_12 (QE, not_3_out, or_2_out);
  or or_9 (QF, and_8_out, and_9_out, I3);
  or or_10 (QG, and_10_out, and_11_out, I3);
endmodule

// 1-12
module _1_12_Counter (
  input  Clk_In,
  input  RESET,
  output Q3,
  output Q2,
  output Q1,
  output Q0,
  output AM___PM_Toggle
);

  wire and_1_out, and_2_out, and_3_out, and_4_out, and_5_out, or_1_out, or_2_out;

  and and_1 (and_1_out, Q1, Q2, Q0);
  and and_2 (and_2_out, Q2, Q3);
  T_Flip_Flop t_ff_1 (.clk(and_3_out), .T(1'b1), .Q(AM___PM_Toggle));  // open: Qn, preset, reset, en
  or or_1 (or_1_out, and_1_out, and_2_out);
  and and_3 (and_3_out, Q3, Q2);
  T_Flip_Flop t_ff_2 (.clk(Clk_In), .T(or_1_out), .Q(Q3), .reset(RESET));  // open: Qn, preset, en
  and and_4 (and_4_out, Q2, Q3);
  or or_2 (or_2_out, and_4_out, and_5_out);
  and and_5 (and_5_out, Q0, Q1);
  T_Flip_Flop t_ff_3 (.clk(Clk_In), .T(or_2_out), .Q(Q2), .reset(RESET));  // open: Qn, preset, en
  T_Flip_Flop t_ff_4 (.clk(Clk_In), .T(Q0), .Q(Q1), .reset(RESET));  // open: Qn, preset, en
  T_Flip_Flop t_ff_5 (.clk(Clk_In), .T(1'b1), .Q(Q0), .reset(RESET));  // open: Qn, preset, en
endmodule

// Decoder
module Hour_Decoder (
  input  I3,
  input  I2,
  input  I1,
  input  I0,
  output QA1,
  output QB1,
  output QC1,
  output QD1,
  output QE1,
  output QF1,
  output QG1,
  output QA0,
  output QB0,
  output QC0,
  output QD0,
  output QE0,
  output QF0,
  output QG0
);

  wire and_1_out, not_1_out, not_2_out, not_3_out, not_4_out, or_2_out, or_3_out, or_4_out, or_5_out,
       or_6_out, or_7_out, or_8_out, or_9_out, or_10_out, or_11_out, or_12_out, or_13_out, or_14_out,
       or_15_out, or_16_out, or_17_out, or_18_out, or_19_out, or_20_out;

  not not_1 (not_1_out, I3);
  not not_2 (not_2_out, I0);
  not not_3 (not_3_out, I1);
  not not_4 (not_4_out, I2);
  or or_1 (QA1, not_1_out, and_1_out);
  and and_1 (and_1_out, not_3_out, not_4_out);
  or or_2 (or_2_out, not_2_out, not_3_out, not_1_out);
  or or_3 (or_3_out, I0, I1, not_4_out, I3);
  or or_4 (or_4_out, not_2_out, I1, I2, I3);
  or or_5 (or_5_out, I0, not_3_out, not_4_out);
  and and_2 (QB0, or_5_out, or_6_out);
  or or_6 (or_6_out, not_2_out, I1, not_4_out);
  or or_7 (or_7_out, not_4_out, not_1_out);
  or or_8 (or_8_out, I0, not_3_out, I2, I3);
  or or_9 (or_9_out, not_2_out, not_1_out);
  or or_10 (or_10_out, not_2_out, not_3_out, not_4_out);
  or or_11 (or_11_out, not_2_out, I1, I2);
  or or_12 (or_12_out, I0, I1, not_4_out, I3);
  or or_13 (or_13_out, I1, not_4_out, I3);
  or or_14 (or_14_out, not_4_out, not_1_out);
  or or_15 (or_15_out, not_2_out, not_3_out);
  or or_16 (or_16_out, not_3_out, I2, I3);
  or or_17 (or_17_out, not_2_out, I2, I3);
  or or_18 (or_18_out, not_3_out, not_1_out);
  or or_19 (or_19_out, not_2_out, not_3_out, not_4_out);
  and and_3 (QG0, or_18_out, or_19_out, or_20_out);
  or or_20 (or_20_out, I1, I2, I3);
  and and_4 (QA0, or_2_out, or_3_out, or_4_out);
  and and_5 (QC0, or_7_out, or_8_out);
  and and_6 (QD0, or_9_out, or_10_out, or_11_out, or_12_out);
  and and_7 (QE0, not_2_out, or_13_out);
  and and_8 (QF0, or_14_out, or_15_out, or_16_out, or_17_out);

  assign QB1 = 1'b1;
  assign QC1 = 1'b1;
  assign QD1 = QA1;
  assign QE1 = QA1;
  assign QF1 = QA1;
  assign QG1 = 1'b0;
endmodule

// 0-6
module _0_6_Counter (
  input  Clk_In,
  input  RESET,
  output Q2,
  output Q1,
  output Q0,
  output Clk_Out
);

  wire and_1_out, and_3_out, or_1_out, or_2_out, or_3_out, t_ff_1_qn, t_ff_2_qn, t_ff_3_qn;

  and and_1 (and_1_out, Q1, or_1_out);
  or or_1 (or_1_out, Q2, Q0);
  and and_2 (Clk_Out, t_ff_1_qn, t_ff_2_qn, t_ff_3_qn);
  T_Flip_Flop t_ff_1 (.clk(Clk_In), .T(and_1_out), .Q(Q2), .Qn(t_ff_1_qn), .reset(RESET));  // open: preset, en
  or or_2 (or_2_out, Q0, and_3_out);
  and and_3 (and_3_out, Q2, Q1);
  T_Flip_Flop t_ff_2 (.clk(Clk_In), .T(or_2_out), .Q(Q1), .Qn(t_ff_2_qn), .reset(RESET));  // open: preset, en
  or or_3 (or_3_out, t_ff_2_qn, t_ff_1_qn);
  T_Flip_Flop t_ff_3 (.clk(Clk_In), .T(or_3_out), .Q(Q0), .Qn(t_ff_3_qn), .reset(RESET));  // open: preset, en
endmodule

// Decoder
module Day_Decoder (
  input  I2,
  input  I1,
  input  I0,
  output Q0,
  output Q1,
  output Q2,
  output Q3,
  output Q4,
  output Q5,
  output Q6,
  output Q7
);

  wire not_1_out, not_2_out, not_3_out, not_4_out, not_5_out, not_6_out, not_7_out, not_8_out, not_9_out,
       not_10_out, not_11_out, not_12_out;

  not not_1 (not_1_out, I2);
  not not_2 (not_2_out, I1);
  not not_3 (not_3_out, I0);
  not not_4 (not_4_out, I2);
  not not_5 (not_5_out, I1);
  not not_6 (not_6_out, I2);
  not not_7 (not_7_out, I0);
  not not_8 (not_8_out, I2);
  not not_9 (not_9_out, I1);
  not not_10 (not_10_out, I0);
  not not_11 (not_11_out, I1);
  not not_12 (not_12_out, I0);
  and and_1 (Q7, I2, I1, I0);
  and and_2 (Q0, not_1_out, not_2_out, not_3_out);
  and and_3 (Q1, not_4_out, not_5_out, I0);
  and and_4 (Q2, not_6_out, I1, not_7_out);
  and and_5 (Q3, not_8_out, I1, I0);
  and and_6 (Q4, I2, not_9_out, not_10_out);
  and and_7 (Q5, I2, not_11_out, I0);
  and and_8 (Q6, I2, I1, not_12_out);
endmodule

module CLOCK (
  input  CLK_IN,
  input  Set_Days,
  input  Set_Hours,
  input  Set_Minutes,
  input  RESET,
  output Fri,
  output Thrus,
  output out_8,
  output out_9,
  output out_10,
  output out_11,
  output out_12,
  output out_13,
  output out_14,
  output out_15,
  output out_16,
  output out_17,
  output out_18,
  output out_19,
  output out_20,
  output out_21,
  output out_22,
  output out_23,
  output out_24,
  output out_25,
  output out_26,
  output out_27,
  output out_28,
  output out_29,
  output out_30,
  output out_31,
  output Wends,
  output Tues,
  output out_34,
  output out_35,
  output out_36,
  output out_37,
  output out_38,
  output out_39,
  output out_40,
  output out_41,
  output out_42,
  output out_43,
  output out_44,
  output out_45,
  output out_46,
  output out_47,
  output out_48,
  output out_49,
  output out_50,
  output out_51,
  output Mon,
  output AM,
  output PM,
  output Sun,
  output Sat,
  output AM_2,
  output Q3,
  output Q2,
  output Q1,
  output Q0,
  output s1,
  output s0,
  output m2,
  output m0,
  output m1,
  output s3,
  output s2
);

  wire n0_5_counter_1_clk_out, n0_5_counter_1_q1, n0_5_counter_2_clk_out, n0_5_counter_2_q0,
       n0_5_counter_2_q1, n0_5_counter_2_q2, n0_6_counter_1_q0, n0_6_counter_1_q1, n0_6_counter_1_q2,
       n0_9_counter_1_clk_out, n0_9_counter_2_clk_out, n0_9_counter_2_q0, n0_9_counter_2_q1,
       n0_9_counter_2_q2, n0_9_counter_2_q3, n1_12_counter_1_am___pm_toggle, xor_1_out, xor_2_out, xor_3_out;

  Day_Decoder day_decoder_1 (
    .I2(n0_6_counter_1_q2), .I1(n0_6_counter_1_q1), .I0(n0_6_counter_1_q0), .Q0(Sat), .Q1(Sun), .Q2(Mon),
    .Q3(Tues), .Q4(Wends), .Q5(Thrus), .Q6(Fri));  // open: Q7
  _0_6_Counter u_0_6_counter_1 (
    .Clk_In(xor_1_out), .Q2(n0_6_counter_1_q2), .Q1(n0_6_counter_1_q1), .Q0(n0_6_counter_1_q0));  // open: Clk_Out, RESET
  xor xor_1 (xor_1_out, AM, Set_Days);
  Hour_Decoder hour_decoder_1 (
    .QA1(out_10), .QB1(out_11), .QC1(out_36), .QD1(out_35), .QE1(out_34), .QF1(out_9), .QG1(out_8),
    .QA0(out_14), .QB0(out_15), .QC0(out_39), .QD0(out_38), .QE0(out_37), .QF0(out_13), .QG0(out_12),
    .I3(Q3), .I2(Q2), .I1(Q1), .I0(Q0));
  Decoder #(.disabled(0), .enable("false")) decoder_1 (.out0(AM), .out1(PM), .sel(n1_12_counter_1_am___pm_toggle));
  xor xor_2 (xor_2_out, n0_5_counter_1_clk_out, Set_Hours);
  _1_12_Counter u_1_12_counter_1 (
    .Q3(Q3), .Q2(Q2), .Q1(Q1), .Q0(Q0), .Clk_In(xor_2_out), .AM___PM_Toggle(n1_12_counter_1_am___pm_toggle),
    .RESET(RESET));
  Binary_to_7_Seg_Decoder binary_to_7_seg_decoder_1 (
    .QA(out_18), .QB(out_19), .QC(out_42), .QD(out_41), .QE(out_40), .QF(out_17), .QG(out_16), .I3(1'b0),
    .I2(m2), .I1(n0_5_counter_1_q1), .I0(m0));
  Binary_to_7_Seg_Decoder binary_to_7_seg_decoder_2 (
    .QA(out_22), .QB(out_23), .QC(out_45), .QD(out_44), .QE(out_43), .QF(out_21), .QG(out_20), .I3(s3),
    .I2(s2), .I1(s1), .I0(s0));
  _0_5_Counter u_0_5_counter_1 (
    .Clk_Out(n0_5_counter_1_clk_out), .Clk_In(n0_9_counter_1_clk_out), .RESET(RESET), .Q2(m2),
    .Q1(n0_5_counter_1_q1), .Q0(m0));
  xor xor_3 (xor_3_out, n0_5_counter_2_clk_out, Set_Minutes);
  _0_9_Counter u_0_9_counter_1 (
    .Clk_Out(n0_9_counter_1_clk_out), .Clk_In(xor_3_out), .RESET(RESET), .Q3(s3), .Q2(s2), .Q1(s1), .Q0(s0));
  Binary_to_7_Seg_Decoder binary_to_7_seg_decoder_3 (
    .QA(out_26), .QB(out_27), .QC(out_48), .QD(out_47), .QE(out_46), .QF(out_25), .QG(out_24), .I3(1'b0),
    .I2(n0_5_counter_2_q2), .I1(n0_5_counter_2_q1), .I0(n0_5_counter_2_q0));
  Binary_to_7_Seg_Decoder binary_to_7_seg_decoder_4 (
    .QA(out_30), .QB(out_31), .QC(out_51), .QD(out_50), .QE(out_49), .QF(out_29), .QG(out_28),
    .I3(n0_9_counter_2_q3), .I2(n0_9_counter_2_q2), .I1(n0_9_counter_2_q1), .I0(n0_9_counter_2_q0));
  _0_5_Counter u_0_5_counter_2 (
    .Clk_Out(n0_5_counter_2_clk_out), .Clk_In(n0_9_counter_2_clk_out), .RESET(RESET), .Q2(n0_5_counter_2_q2),
    .Q1(n0_5_counter_2_q1), .Q0(n0_5_counter_2_q0));
  _0_9_Counter u_0_9_counter_2 (
    .Clk_Out(n0_9_counter_2_clk_out), .Clk_In(CLK_IN), .RESET(RESET), .Q3(n0_9_counter_2_q3),
    .Q2(n0_9_counter_2_q2), .Q1(n0_9_counter_2_q1), .Q0(n0_9_counter_2_q0));

  assign AM_2 = AM;
  assign m1 = m0;
endmodule

// ALARM_COMP
module Alarm (
  input  ON_OFF,
  input  Q3,
  input  Q2,
  input  Q1,
  input  Set_Hours,
  input  Q0,
  input  M2,
  input  M1,
  input  RESET,
  input  M0,
  input  S3,
  input  S2,
  input  S1,
  input  Set_Minutes,
  input  S0,
  input  Am_IN,
  output AM,
  output PM,
  output q0_2,
  output q1_2,
  output q2_2,
  output q3_2,
  output m0_2,
  output m1_2,
  output m2_2,
  output OUT,
  output s0_2,
  output s1_2,
  output s2_2,
  output s3_2
);

  wire and_1_out, and_2_out, and_3_out, n0_9_counter_1_clk_out, n1_12_counter_1_am___pm_toggle, not_1_out,
       or_1_out, xnor_1_out, xnor_2_out, xnor_3_out, xnor_4_out, xnor_5_out, xnor_6_out, xnor_7_out,
       xnor_8_out, xnor_9_out, xnor_10_out, xnor_11_out;

  Decoder #(.enable("false")) decoder_1 (.out0(AM), .out1(PM), .sel(n1_12_counter_1_am___pm_toggle));
  _1_12_Counter u_1_12_counter_1 (
    .Q3(q3_2), .Q2(q2_2), .Q1(q1_2), .Q0(q0_2), .Clk_In(Set_Hours),
    .AM___PM_Toggle(n1_12_counter_1_am___pm_toggle), .RESET(RESET));
  _0_5_Counter u_0_5_counter_1 (
    .Clk_In(n0_9_counter_1_clk_out), .RESET(RESET), .Q2(m2_2), .Q1(m1_2), .Q0(m0_2));  // open: Clk_Out
  _0_9_Counter u_0_9_counter_1 (
    .Clk_Out(n0_9_counter_1_clk_out), .Clk_In(Set_Minutes), .RESET(RESET), .Q3(s3_2), .Q2(s2_2), .Q1(s1_2),
    .Q0(s0_2));
  not not_1 (not_1_out, Am_IN);
  xnor xnor_1 (xnor_1_out, q3_2, Q3);
  xnor xnor_2 (xnor_2_out, q2_2, Q2);
  xnor xnor_3 (xnor_3_out, q1_2, Q1);
  xnor xnor_4 (xnor_4_out, q0_2, Q0);
  xnor xnor_5 (xnor_5_out, m2_2, M2);
  xnor xnor_6 (xnor_6_out, m1_2, M1);
  xnor xnor_7 (xnor_7_out, m0_2, M0);
  xnor xnor_8 (xnor_8_out, s3_2, S3);
  xnor xnor_9 (xnor_9_out, s2_2, S2);
  xnor xnor_10 (xnor_10_out, s1_2, S1);
  xnor xnor_11 (xnor_11_out, s0_2, S0);
  and and_1 (and_1_out, Am_IN, AM);
  and and_2 (and_2_out, not_1_out, PM);
  or or_1 (or_1_out, and_1_out, and_2_out);
  and and_3 (and_3_out, xnor_1_out, xnor_2_out, xnor_3_out, xnor_4_out, xnor_5_out, xnor_6_out, xnor_7_out, xnor_8_out, xnor_9_out, xnor_10_out, xnor_11_out, or_1_out);
  and and_4 (OUT, ON_OFF, and_3_out);
endmodule
